# Fritzing sketch schematic files with arduino2 (saved by Fritzing 0.9.3b)
breadboards: 1

parts:
  Nokia_5110_LCD_Module1 = Nokia 5110 LCD
  Raspberry_Pi_1 = Raspberry Pi 3 [part_number=RPI-3-V1.2]
  IC1 = L293D [package=THT]
  U1 = POT [package=pot_alpha_rv16af-20]
  U2 = Module 4 Relais 5V [package="Module 4 Relais 5V"]
  M1 = DC Motor
  J2 = Power Jack [package=power_jack_slot]
  Part2 = Arduino Nano (Rev3.0)
  R3 = Resistor [tolerance=±5% resistance=220 package="2010 [SMD]"]
  R4 = Resistor [tolerance=±5% resistance=220 package="2010 [SMD]"]
  R5 = Resistor [tolerance=±5% resistance=220 package="2010 [SMD]"]

nets:
  N1: Nokia_5110_LCD_Module1.VCC, Raspberry_Pi_1.GIPO24
  N2: Nokia_5110_LCD_Module1.GND, Raspberry_Pi_1.GIPO8
  N3: Nokia_5110_LCD_Module1.SCE, Raspberry_Pi_1.GIPO23
  N4: Nokia_5110_LCD_Module1.RST, Nokia_5110_LCD_Module1.RST_(out), Raspberry_Pi_1.GIPO10
  N5: Nokia_5110_LCD_Module1.D/C, Nokia_5110_LCD_Module1.D/C_(out), Raspberry_Pi_1.GIPO11
  3V3: Nokia_5110_LCD_Module1.DN(MOSI), Raspberry_Pi_1.3v3, Raspberry_Pi_1.3V3
  N6: Nokia_5110_LCD_Module1.SCLK, Raspberry_Pi_1.GIPO18
  GND: Nokia_5110_LCD_Module1.LED, Nokia_5110_LCD_Module1.LED_(out), Raspberry_Pi_1.GND, IC1.0V, U1.A, U2.GND, J2.GNDBREAK, Part2.GND, R3.Pin_1
  N7: Raspberry_Pi_1.GIPO17, IC1.Enable_1
  N8: Raspberry_Pi_1.GIPO27, IC1.In_1
  N9: Raspberry_Pi_1.GIPO22, IC1.In_2
  N10: Raspberry_Pi_1.GIPO5, U2.IN4
  N11: Raspberry_Pi_1.GIPO6, U2.IN3
  N12: Raspberry_Pi_1.GIPO19, U2.IN2
  N13: Raspberry_Pi_1.GIPO26, U2.IN1
  N14: Raspberry_Pi_1.GIPO15, R3.Pin_0, R4.Pin_1, R5.Pin_1
  N15: Raspberry_Pi_1.GIPO14, Part2.D0/RX
  5V: Raspberry_Pi_1.5V, U1.E, Part2.5V
  N16: IC1.Out_1_(_Controlled_by_Enable_1_), M1.pin_2
  N17: IC1.Out_2_(_Controlled_by_Enable_1_), M1.pin_1
  N18: IC1.+Vmotor, IC1.+V, U2.VCC, J2.PWR
  N19: U1.S, Part2.A0
  N20: U2.JD-VCC, U2.VCC2
  N21: Part2.D1/TX, R4.Pin_0, R5.Pin_0

custom parts:
  Nokia 5110 LCD: Nokia 5110 Graphic 84*48 LCD module such as the Sparkfun LCD-10168 or the clones from Ebay. There is example code for the Arduino available from the Sparkfun site in https://learn.sparkfun.com/tutorials/graphic-lcd-hookup-guide This is a 3.3V device, if you are running it from a 5V micro you need a 5V tolorant level translator such as the 74ahc367 to protect the signal imputs. Rafa G. did a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
  Module 4 Relais 5V: Module 4 Relais 5V 4x SPD-06VDC-SD-C
