# Fritzing sketch schematic files (saved by Fritzing 0.9.3b)
breadboards: 1

parts:
  Nokia_5110_LCD_Module1 = Nokia 5110 LCD
  Part1 = Adafruit ADS1015 12Bit I2C ADC [part_number="Adafruit #1083"]
  Raspberry_Pi_1 = Raspberry Pi 3 [part_number=RPI-3-V1.2]
  IC1 = L293D [package=THT]
  U1 = POT [package=pot_alpha_rv16af-20]
  U2 = Module 4 Relais 5V [package="Module 4 Relais 5V"]
  M1 = DC Motor
  J2 = Power Jack [package=power_jack_slot]

nets:
  N1: Nokia_5110_LCD_Module1.VCC, Raspberry_Pi_1.GIPO24
  N2: Nokia_5110_LCD_Module1.GND, Raspberry_Pi_1.GIPO8
  N3: Nokia_5110_LCD_Module1.SCE, Raspberry_Pi_1.GIPO23
  N4: Nokia_5110_LCD_Module1.RST, Nokia_5110_LCD_Module1.RST_(out), Raspberry_Pi_1.GIPO10
  N5: Nokia_5110_LCD_Module1.D/C, Nokia_5110_LCD_Module1.D/C_(out), Raspberry_Pi_1.GIPO11
  3V3: Nokia_5110_LCD_Module1.DN(MOSI), Nokia_5110_LCD_Module1.DN(MODI)_(out), Part1.VDD, Raspberry_Pi_1.3v3, Raspberry_Pi_1.3V3, U1.E
  N6: Nokia_5110_LCD_Module1.SCLK, Raspberry_Pi_1.GIPO18
  GND: Nokia_5110_LCD_Module1.LED, Nokia_5110_LCD_Module1.LED_(out), Part1.GND, Raspberry_Pi_1.GND, IC1.0V, U2.GND, J2.GNDBREAK
  N7: Part1.AIN0, U1.S
  N8: Part1.SDA, Raspberry_Pi_1.GPIO2
  N9: Part1.SCL, Raspberry_Pi_1.GPIO3
  N10: Raspberry_Pi_1.GIPO17, IC1.Enable_1
  N11: Raspberry_Pi_1.GIPO27, IC1.In_1
  N12: Raspberry_Pi_1.GIPO22, IC1.In_2
  N13: Raspberry_Pi_1.GIPO5, U2.IN4
  N14: Raspberry_Pi_1.GIPO6, U2.IN3
  N15: Raspberry_Pi_1.GIPO19, U2.IN2
  N16: Raspberry_Pi_1.GIPO26, U2.IN1
  N17: IC1.Out_1_(_Controlled_by_Enable_1_), M1.pin_2
  N18: IC1.Out_2_(_Controlled_by_Enable_1_), M1.pin_1
  N19: IC1.+Vmotor, IC1.+V, U2.VCC, J2.PWR
  N20: U2.JD-VCC, U2.VCC2

custom parts:
  Nokia 5110 LCD: Nokia 5110 Graphic 84*48 LCD module such as the Sparkfun LCD-10168 or the clones from Ebay. There is example code for the Arduino available from the Sparkfun site in https://learn.sparkfun.com/tutorials/graphic-lcd-hookup-guide This is a 3.3V device, if you are running it from a 5V micro you need a 5V tolorant level translator such as the 74ahc367 to protect the signal imputs. Rafa G. did a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
  Adafruit ADS1015 12Bit I2C ADC: For microcontrollers without an analog-to-digital converter or when you want a higher-precision ADC, the ADS1015 provides 12-bit precision at 3300 samples/second over I2C. The chip can be configured as 4 single-ended input channels, or two differential channels. As a nice bonus, it even includes a programmable gain amplifier, up to x16, to help boost up smaller single/differential signals to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
  Module 4 Relais 5V: Module 4 Relais 5V 4x SPD-06VDC-SD-C
